# Fritzing sketch wiring (saved by Fritzing 0.9.10b)
breadboards: 1

parts:
  C2 = Electrolytic Capacitor [capacitance=1000µF voltage=6.3V package="300 mil [THT, electrolytic]"]
  R1 = Resistor [tolerance=±5% resistance=470 package="0603 [SMD]"]
  Part1 = Arduino Uno (Rev3)
  U1 = Mini-USB _B_ connector with 5th pin broken out. [package=usb-micro_b]
  S1 = Round Pushbutton
  S2 = Round Pushbutton
  S3 = Round Pushbutton
  S4 = Round Pushbutton
  S5 = Round Pushbutton
  LED1 = smd LED [color="Red (633nm)" package="1206 [SMD]"]
  LED2 = smd LED [color="White (4500K)" package="1206 [SMD]"]
  LED3 = smd LED [color="Green (555nm)" package="1206 [SMD]"]
  LED4 = smd LED [color="Blue (470nm)" package="1206 [SMD]"]
  LED5 = smd LED [color="Yellow (585nm)" package="1206 [SMD]"]
  right_eye1 = 12 NeoPixel Ring [part_number=1643]
  right_eye2 = 12 NeoPixel Ring [part_number=1643]
  VCC1 = 4 x AAA Battery Mount

nets:
  GND: C2.-, Part1.GND, U1.D-, S1.leg1, S2.leg1, S3.leg1, S4.leg1, S5.leg1, LED1.anode, LED2.anode, LED3.anode, LED4.anode, LED5.anode, right_eye1.GND, right_eye2.GND, VCC1.-
  VDD: C2.+, U1.VBUS, right_eye1.VDD, right_eye2.VDD, VCC1.+
  N1: R1.Pin_0, Part1.D13/SCK
  N2: R1.Pin_1, right_eye1.IN, right_eye2.IN
  N3: Part1.D8, S4.leg0
  N4: Part1.D9_PWM, S3.leg0
  N5: Part1.D10_PWM/SS, LED2.cathode
  N6: Part1.D11_PWM/MOSI, S1.leg0
  N7: Part1.D2, S2.leg0
  N8: Part1.D3_PWM, LED1.cathode
  N9: Part1.D4, S5.leg0
  N10: Part1.D5_PWM, LED5.cathode
  N11: Part1.D6_PWM, LED3.cathode
  N12: Part1.D7, LED4.cathode

custom parts:
  12 NeoPixel Ring: 12 ultra bright smart LED NeoPixels are arranged in a circle with 1.5" (37mm) outer diameter. The rings are 'chainable' - connect the output pin of one to the input pin of another. Use only one microcontroller pin to control as many as you can chain together! Each LED is addressable as the driver chip is inside the LED. Each one has ~18mA constant current drive so the color will be very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
